# Fritzing sketch LumineaterBot (saved by Fritzing 0.8.7b)
breadboards: 1

parts:
  TRINKET1 = Trinket 5V
  R1 = Photocell (LDR) [package=THT]
  R2 = Photocell (LDR) [package=THT]
  Servo_L = Basic Servo
  Servo_R = Basic Servo
  R3 = Resistor [tolerance=±5% resistance=10k package=THT]
  R4 = Resistor [tolerance=±5% resistance=10k package=THT]
  S1 = SWITCH-DPDT [package=eg2211]
  VCC1 = Battery block 9V

nets:
  VCC: TRINKET1.no_name_yet#1, Servo_L.vcc, Servo_R.vcc, S1.1
  GND: TRINKET1.no_name_yet#2, Servo_L.gnd, Servo_R.gnd, R3.Pin_1, R4.Pin_0, VCC1.-
  N1: TRINKET1.no_name_yet#3, R2.pin_1, R4.Pin_1
  N2: TRINKET1.no_name_yet#6, R1.pin_1, R2.pin_0
  N3: TRINKET1.no_name_yet#7, R1.pin_0, R3.Pin_0
  N4: TRINKET1.no_name_yet#8, Servo_L.pulse
  N5: TRINKET1.no_name_yet#9, Servo_R.pulse
  N6: S1.2, VCC1.+

custom parts:
  Trinket 5V: Adafruit Trinket 5V
